# Fritzing sketch SmartStation_V9_circuit (saved by Fritzing 0.9.3b)
circuit board: 8.46667cm x 5.64444cm

parts:
  ESP-12 = Gizwits WiFi Witty ESP-12F
  Power_plug1 = Power plug
  Blind_Motor = DC Motor
  TEMPERATURE_SENSOR_FAN = Fan - Ventilador [package=THT]
  M2 = RioRand LM2596
  OLED_Display = Grove OLED 128x96
  PIR1 = PIR sensor
  DS1 = DS18B20 1-Wire Temperature Sensor [part_number=DS18B20]
  BC547 = PNP-Transistor [package="TO92 [THT]"]
  IR_LED = LTE-302 [package=lte-302]
  R1 = Resistor [tolerance=±5% resistance=4.7k package="0402 [SMD]"]
  S1 = H-Bridge with L298N
  U1 = Molex Picoblade Series Header [part_number=0533980471 package=Picoblade-53398-0471]
  U3 = Molex Picoblade Series Header [part_number=0533980271 package=Picoblade-53398-0271]
  U2 = Molex Picoblade Series Header [part_number=0533980571 package=Picoblade-53398-0571]
  WS2812B = DUO LED RG [package="5 mm [THT]"]
  S2 = Pushbutton [package="[SMD]"]
  R3 = Resistor [tolerance=±5% resistance=10k package=THT]

nets (from the breadboard view):
  VCC: ESP-12.CH_PD, ESP-12.VCC, M2.Pin_3, OLED_Display.VCC, DS1.VDD, IR_LED.C, R1.Pin_1, U2.3, R3.Pin_0
  N1: ESP-12.GPIO16, PIR1.SIG
  N2: ESP-12.GPIO14, S2.Pin_3, R3.Pin_1
  N3: ESP-12.GPIO12, BC547.B
  N4: ESP-12.GPIO13, DS1.DQ, R1.Pin_0, U2.2
  GND: ESP-12.GND, M2.Pin_4, OLED_Display.GND, DS1.GND, BC547.E, U1.4, U2.1, S2.Pin_1
  N5: ESP-12.GPIO15, S1.IN2
  N6: ESP-12.GPIO2, S1.IN1
  N7: ESP-12.GPIO0, S1.ENB, U1.3
  N8: ESP-12.GPIO4, OLED_Display.SDA
  N9: ESP-12.GPIO5, OLED_Display.SCL
  N10: ESP-12.RXD, U1.2, WS2812B.common_cathode
  N11: ESP-12.TXD, U1.1
  GND_2: Power_plug1.GND, M2.Pin_2, PIR1.GND, S1.GND, WS2812B.green_anode
  VCC_2: Power_plug1.VCC, M2.Pin_1, S1.12V
  N12: Blind_Motor.pin_1, S1.M1-02, U3.1
  N13: Blind_Motor.pin_2, S1.M1-01, U3.2
  N14: TEMPERATURE_SENSOR_FAN.5V, S1.M2-01, U2.4
  N15: TEMPERATURE_SENSOR_FAN.GND, S1.M2-02, U2.5
  VDD: PIR1.VDD, S1.5V, WS2812B.red_anode
  N16: BC547.C, IR_LED.A
  N17: S1.ENA, S1.ENA-5V
  N18: S1.IN4, S1.ENB-5V

custom parts:
  Fan - Ventilador: Ventilador de 2 pines, se encuentra comunmente en computadoras de escritorio
  H-Bridge with L298N: h-bridge
